// Logisim project Task_01 (a).circ as structural Verilog: 1 circuit, main circuit main
module main (
  input  A,
  input  B,
  input  C,
  input  E,
  input  in_5,
  output ABC__D_prime___E_prime
);

  wire nand_1_out, nand_2_out, nand_3_out, nand_4_out, nand_5_out, nand_6_out, nand_7_out;

  nand nand_1 (nand_1_out, A, B);
  not nand_2 (nand_2_out, C);  // NAND_Gate
  nand nand_3 (nand_3_out, E, in_5);
  nand nand_4 (nand_4_out, nand_1_out, nand_1_out, nand_1_out);
  nand nand_5 (nand_5_out, nand_2_out, nand_2_out);
  nand nand_6 (nand_6_out, nand_3_out, nand_3_out);
  nand nand_7 (nand_7_out, nand_4_out, nand_5_out);
  nand nand_8 (ABC__D_prime___E_prime, nand_7_out, nand_6_out);

  // Notes on the sheet:
  //   A'B'
  //   C'
  //   D'
  //   AB
  //   C
  //   D
  //   ABC
endmodule
