// Logisim project Task_01 (b).circ as structural Verilog: 1 circuit, main circuit main
module main (
  input  A,
  input  B,
  input  C,
  input  D,
  input  E,
  output ABC___DE
);

  wire nand_1_out, nand_2_out, nand_3_out, nand_4_out, nand_5_out, nand_6_out;

  nand nand_1 (nand_1_out, A, B);
  not nand_2 (nand_2_out, C);  // NAND_Gate
  nand nand_3 (nand_3_out, D, E);
  nand nand_4 (nand_4_out, nand_1_out, nand_1_out);
  nand nand_5 (nand_5_out, nand_2_out, nand_2_out);
  nand nand_6 (nand_6_out, nand_4_out, nand_5_out);
  nand nand_7 (ABC___DE, nand_6_out, nand_3_out);

  // Notes on the sheet:
  //   AB
  //   C
  //   D
  //   ABC
endmodule
