// Logisim project Task_02.circ as structural Verilog: 1 circuit, main circuit main
module main (
  input  B,
  input  C,
  input  A,
  output BC___AC___B_prime_C_prime
);

  wire and_1_out, and_2_out, and_3_out, and_4_out, and_5_out, and_6_out, not_1_out, not_2_out;

  buf and_1 (and_1_out, B);  // AND_Gate
  buf and_2 (and_2_out, C);  // AND_Gate
  buf and_3 (and_3_out, A);  // AND_Gate
  not not_1 (not_1_out, and_2_out);
  and and_4 (and_4_out, and_2_out, and_3_out);
  not not_2 (not_2_out, and_1_out);
  and and_5 (and_5_out, and_1_out, and_2_out);
  and and_6 (and_6_out, not_2_out, not_1_out);
  or or_1 (BC___AC___B_prime_C_prime, and_5_out, and_6_out, and_4_out);

  // Notes on the sheet:
  //   AC
  //   B'
  //   BC
  //   b'c'
endmodule
