// Logisim project Task_03 (a).circ as structural Verilog: 1 circuit, main circuit main
module main (
  input  A,
  input  B,
  input  C,
  input  A_2,
  input  B_2,
  input  C_2,
  output out_7,
  output out_8
);

  wire and_1_out, and_2_out, and_3_out, and_4_out, and_5_out, not_1_out, not_2_out, not_3_out, not_4_out,
       not_5_out, not_6_out;

  and and_1 (and_1_out, A_2, C_2);
  not not_1 (not_1_out, A_2);
  and and_2 (and_2_out, not_1_out, not_2_out);
  not not_2 (not_2_out, C_2);
  not not_3 (not_3_out, B_2);
  not not_4 (not_4_out, A);
  not not_5 (not_5_out, B);
  not not_6 (not_6_out, C);
  and and_3 (and_3_out, not_4_out, not_5_out, not_6_out);
  and and_4 (and_4_out, B, C);
  and and_5 (and_5_out, A, B);
  or or_1 (out_8, and_1_out, and_2_out, not_3_out);
  or or_2 (out_7, and_3_out, and_4_out, and_5_out);

  // Notes on the sheet:
  //   PART #02
  //   PART #01
endmodule
