// Logisim project Task_03 (b).circ as structural Verilog: 1 circuit, main circuit main
module main (
  input  A,
  input  B,
  input  C,
  input  D,
  input  D_2,
  input  C_2,
  input  B_2,
  input  A_2,
  output out_9,
  output out_10
);

  wire and_1_out, and_2_out, and_3_out, and_4_out, and_5_out, not_1_out, not_2_out, not_3_out, not_4_out,
       not_5_out, not_6_out, not_7_out;

  not not_1 (not_1_out, C_2);
  not not_2 (not_2_out, A);
  and and_1 (and_1_out, not_2_out, not_3_out);
  not not_3 (not_3_out, C);
  not not_4 (not_4_out, A);
  and and_2 (and_2_out, not_4_out, B);
  and and_3 (and_3_out, A, not_5_out, D);
  not not_5 (not_5_out, B);
  and and_4 (and_4_out, not_1_out, B_2);
  not not_6 (not_6_out, B_2);
  and and_5 (and_5_out, C_2, not_6_out, A_2);
  not not_7 (not_7_out, D_2);
  or or_1 (out_9, and_1_out, and_2_out, and_3_out);
  or or_2 (out_10, not_7_out, and_4_out, and_5_out);

  // Notes on the sheet:
  //   PART #01
  //   PART #02
endmodule
