// Logisim project Task_03.circ as structural Verilog: 1 circuit, main circuit main
module main (
  input  B_star,
  input  B1,
  input  A_star,
  input  A1,
  output A___B,
  output A___B_2,
  output A_B
);

  wire and_1_out, and_2_out, and_3_out, and_4_out, and_5_out, and_6_out, and_7_out, and_8_out, and_9_out,
       and_10_out, not_1_out, not_2_out, not_3_out, not_4_out;

  not not_1 (not_1_out, B_star);
  not not_2 (not_2_out, B1);
  not not_3 (not_3_out, A_star);
  not not_4 (not_4_out, A1);
  and and_1 (and_1_out, B_star, not_4_out, not_3_out);
  and and_2 (and_2_out, B1, not_4_out);
  and and_3 (and_3_out, B_star, B1, not_3_out);
  and and_4 (and_4_out, not_2_out, A1);
  and and_5 (and_5_out, A1, A_star);
  and and_6 (and_6_out, not_1_out, not_2_out, A_star);
  and and_7 (and_7_out, not_1_out, not_2_out, not_3_out, not_4_out);
  and and_8 (and_8_out, B_star, not_2_out, A_star, not_4_out);
  and and_9 (and_9_out, B_star, B1, A_star, A1);
  and and_10 (and_10_out, B_star, B1, not_3_out, A1);
  or or_1 (A___B, and_1_out, and_2_out, and_3_out);
  or or_2 (A___B_2, and_4_out, and_5_out, and_6_out);
  or or_3 (A_B, and_7_out, and_8_out, and_9_out, and_10_out);
endmodule
